# Fritzing sketch P2_Semaforos (saved by Fritzing 0.9.3b)
breadboards: 2

parts:
  Componente1 = Arduino Uno (Rev3)
  LED1 = LED - 5mm [color="Red (633nm)" package="5 mm [THT]"]
  R1 = Resistor [tolerance=±5% resistance=570 package=THT]
  R2 = Resistor [tolerance=±5% resistance=570 package=THT]
  R3 = Resistor [tolerance=±5% resistance=570 package=THT]
  R4 = Resistor [tolerance=±5% resistance=570 package=THT]
  R5 = Resistor [tolerance=±5% resistance=570 package=THT]
  R6 = Resistor [tolerance=±5% resistance=570 package=THT]
  LED8 = LED - 5mm [color="Orange (620nm)" package="5 mm [THT]"]
  LED9 = LED - 5mm [color="Green (570nm)" package="5 mm [THT]"]
  LED10 = LED - 5mm [color="Red (633nm)" package="5 mm [THT]"]
  LED12 = LED - 5mm [color="Green (570nm)" package="5 mm [THT]"]
  LED11 = smd LED [color="Red (633nm)" package="0603 [SMD]"]
  LED11_2 = smd LED [color="Orange (612nm)" package="0805 [SMD]"]
  LED13 = LED - 5mm [color="Green (570nm)" package="5 mm [THT]"]
  LED14 = LED - 5mm [color="Green (570nm)" package="5 mm [THT]"]
  R7 = Resistor [tolerance=±5% resistance=570 package=THT]
  R8 = Resistor [tolerance=±5% resistance=570 package=THT]
  S2 = Momentary Switch [package=ksa_sealed_tac_switch]
  S3 = Momentary Switch [package=ksa_sealed_tac_switch]
  R9 = Resistor [tolerance=±5% resistance=570 package=THT]
  R10 = Resistor [tolerance=±5% resistance=570 package=THT]

nets:
  N1: Componente1.D8, R1.Pin_1
  N2: Componente1.D10_PWM/SS, R7.Pin_1
  N3: Componente1.D11_PWM/MOSI, R8.Pin_1
  N4: Componente1.D12/MISO, S3.2, R10.Pin_1
  N5: Componente1.GND, R9.Pin_0, R10.Pin_0
  N6: Componente1.D2, S2.2, R9.Pin_1
  N7: Componente1.D3_PWM, R6.Pin_1
  N8: Componente1.D4, R5.Pin_1
  N9: Componente1.D5_PWM, R4.Pin_1
  N10: Componente1.D6_PWM, R3.Pin_1
  N11: Componente1.D7, R2.Pin_1
  N12: Componente1.5V, LED1.anode, LED8.anode, LED9.anode, LED10.anode, LED12.anode, LED11.anode, LED11_2.anode, LED13.anode, LED14.anode, S2.4, S3.4
  N13: LED1.cathode, R6.Pin_0
  N14: R1.Pin_0, LED12.cathode
  N15: R2.Pin_0, LED11.cathode, LED11_2.cathode
  N16: R3.Pin_0, LED10.cathode
  N17: R4.Pin_0, LED9.cathode
  N18: R5.Pin_0, LED8.cathode
  N19: LED13.cathode, R7.Pin_0
  N20: LED14.cathode, R8.Pin_0
