# Fritzing sketch Dados (saved by Fritzing 0.9.3b)
breadboards: 2

parts:
  Componente1 = Arduino Uno (Rev3)
  LED1 = LED - 5mm [color="Green (570nm)" package="5 mm [THT]"]
  LED2 = LED - 5mm [color="Green (570nm)" package="5 mm [THT]"]
  LED3 = LED - 5mm [color="Green (570nm)" package="5 mm [THT]"]
  LED4 = LED - 5mm [color="Green (570nm)" package="5 mm [THT]"]
  LED5 = LED - 5mm [color="Green (570nm)" package="5 mm [THT]"]
  LED6 = LED - 5mm [color="Green (570nm)" package="5 mm [THT]"]
  LED7 = LED - 5mm [color="Green (570nm)" package="5 mm [THT]"]
  R1 = Resistor [tolerance=±5% resistance=570 package="0805 [SMD]"]
  R2 = Resistor [tolerance=±5% resistance=570 package="0805 [SMD]"]
  R3 = Resistor [tolerance=±5% resistance=570 package="0805 [SMD]"]
  R4 = Resistor [tolerance=±5% resistance=570 package="0805 [SMD]"]
  R5 = Resistor [tolerance=±5% resistance=570 package="0805 [SMD]"]
  R6 = Resistor [tolerance=±5% resistance=570 package="0805 [SMD]"]
  R7 = Resistor [tolerance=±5% resistance=570 package="0805 [SMD]"]
  S1 = Pushbutton [package="[THT]"]  # not connected
  R8 = Resistor [tolerance=±5% resistance=570 package="0805 [SMD]"]

nets:
  N1: Componente1.D8, R2.Pin_1
  N2: Componente1.D9_PWM, R1.Pin_1
  N3: Componente1.D11_PWM/MOSI, R8.Pin_0
  N4: Componente1.GND, R8.Pin_1
  N5: Componente1.D3_PWM, R7.Pin_1
  N6: Componente1.D4, R6.Pin_1
  N7: Componente1.D5_PWM, R5.Pin_1
  N8: Componente1.D6_PWM, R4.Pin_1
  N9: Componente1.D7, R3.Pin_1
  N10: Componente1.5V, LED1.anode, LED2.anode, LED3.anode, LED4.cathode, LED5.anode, LED6.anode, LED7.anode
  N11: LED1.cathode, R2.Pin_0
  N12: LED2.cathode, R4.Pin_0
  N13: LED3.cathode, R6.Pin_0
  N14: LED4.anode, R1.Pin_0
  N15: LED5.cathode, R5.Pin_0
  N16: LED6.cathode, R3.Pin_0
  N17: LED7.cathode, R7.Pin_0
