# Fritzing sketch Reproductor (saved by Fritzing 0.9.3b)
breadboards: 2

parts:
  Componente1 = Arduino Uno (Rev3)
  J1 = Piezo Speaker
  U1 = POT [package=3362u]
  S1 = Pushbutton [package="[SMD]"]
  R2 = Resistor [tolerance=±5% resistance=570 package="0805 [SMD]"]

nets:
  N1: Componente1.D8, U1.A
  N2: Componente1.GND, J1.pin1, R2.Pin_1
  N3: Componente1.D3_PWM, S1.Pin_1, S1.Pin_2, R2.Pin_0
  N4: Componente1.5V, U1.S, S1.Pin_3, S1.Pin_4
  N5: J1.pin2, U1.E
