# Fritzing sketch TemperaturaLCD (saved by Fritzing 0.9.3b)
breadboards: 2

parts:
  Componente1 = Arduino Uno (Rev3)
  T1 = LM35 Temperature Sensor [package="TO92 [THT]"]
  U1 = POT [package=3362u]
  LCD1 = LCD screen

nets:
  N1: Componente1.A0, T1.Vout
  N2: Componente1.D11_PWM/MOSI, LCD1.E
  N3: Componente1.D12/MISO, LCD1.RS
  N4: Componente1.D2, LCD1.DB7
  N5: Componente1.D3_PWM, LCD1.DB6
  N6: Componente1.D4, LCD1.DB5
  N7: Componente1.D5_PWM, LCD1.DB4
  5V: Componente1.5V, T1.+Vs, U1.A, LCD1.VDD, LCD1.R/W, LCD1.LED+
  GND: Componente1.GND, T1.GND, U1.E, LCD1.VSS, LCD1.LED-
  N8: U1.S, LCD1.V0
